# Fritzing sketch Sketch (saved by Fritzing 0.9.3b)
breadboards: 1

parts:
  Part1 = InvenSense MPU6050
  U1 = NodeMCU V1.0
  S1 = Pushbutton [package="[THT]"]
  S2 = Pushbutton [package="[THT]"]
  S3 = Pushbutton [package="[THT]"]

nets:
  VCC: Part1.VCC, U1.Vin
  GND: Part1.GND, U1.GND
  N1: Part1.SCL, U1.D6
  N2: Part1.SDA, U1.D5
  N3: S1.Pin_1, S1.Pin_2
  N4: S1.Pin_3, S1.Pin_4
  N5: S2.Pin_1, S2.Pin_2
  N6: S2.Pin_3, S2.Pin_4
  N7: S3.Pin_1, S3.Pin_2
  N8: S3.Pin_3, S3.Pin_4

custom parts:
  NodeMCU V1.0: ESP8266 based NodeMCU
